// Logisim project MDNF.circ as structural Verilog: 1 circuit, main circuit main
module main (
);

  wire and_1_out, and_2_out, and_3_out, and_4_out, and_5_out, and_6_out, and_7_out, not_1_out, not_2_out,
       not_3_out, or_1_out, or_2_out, or_3_out, x0_out, x1_out, x2_out, x3_out;

  Clock #(.highDuration(8), .lowDuration(8)) x3 (.out(x3_out));
  Clock #(.highDuration(4), .lowDuration(4)) x2 (.out(x2_out));
  Clock #(.highDuration(2), .lowDuration(2)) x1 (.out(x1_out));
  Clock x0 (.out(x0_out));
  not not_1 (not_1_out, x2_out);
  not not_2 (not_2_out, x1_out);
  not not_3 (not_3_out, x0_out);
  and and_1 (and_1_out, not_3_out, and_2_out);
  and and_2 (and_2_out, x1_out, not_1_out);
  and and_3 (and_3_out, not_2_out, and_4_out);
  and and_4 (and_4_out, x0_out, x3_out);
  and and_5 (and_5_out, not_3_out, and_6_out);
  and and_6 (and_6_out, not_2_out, x2_out);
  and and_7 (and_7_out, x2_out, x3_out);
  or or_1 (or_1_out, and_5_out, and_7_out);
  or or_2 (or_2_out, and_3_out, or_1_out);
  or or_3 (or_3_out, and_1_out, or_2_out);
  LED led_1 (.in(or_3_out));
endmodule
