// Logisim project Суммирующий счетчик.circ as structural Verilog: 7 circuits, main circuit Суммирующий счетчик с моими триггерами
module \Суммирующий_счетчик_с_моими_триггерами  (
  input  N,
  input  in_2,
  output q0,
  output q1,
  output q2,
  output q3,
  output q4
);

  wire and_1_out, and_2_out, and_3_out, and_4_out, and_5_out, and_6_out, buffer_1_out, or_1_out, plus_1_out,
       Reset_out;

  Button plus_1 (.out(plus_1_out));
  Button Reset (.out(Reset_out));
  and and_1 (and_1_out, plus_1_out, ~N);  // AND_Gate
  buf buffer_1 (buffer_1_out, or_1_out);
  or or_1 (or_1_out, Reset_out, and_6_out);
  \T_триггер  \t_триггер_1  (.T(and_1_out), .Reset(in_2), .nQ(q0), .Q(buffer_1_out));
  and and_2 (and_2_out, q0, ~N);  // AND_Gate
  \T_триггер  \t_триггер_2  (.T(and_2_out), .Reset(in_2), .nQ(q1), .Q(buffer_1_out));
  and and_3 (and_3_out, q1, ~N);  // AND_Gate
  \T_триггер  \t_триггер_3  (.T(and_3_out), .Reset(in_2), .nQ(q2), .Q(buffer_1_out));
  and and_4 (and_4_out, q2, ~N);  // AND_Gate
  \T_триггер  \t_триггер_4  (.T(and_4_out), .Reset(in_2), .nQ(q3), .Q(buffer_1_out));
  and and_5 (and_5_out, q3, ~N);  // AND_Gate
  \T_триггер  \t_триггер_5  (.T(and_5_out), .Reset(in_2), .nQ(q4), .Q(buffer_1_out));
  and and_6 (and_6_out, q4, q1);
endmodule

module \D_триггер  (
  input  D,
  input  c,
  input  Reset,
  output nQ,
  output Q
);

  wire not_1_out;

  not not_1 (not_1_out, D);
  \RS_триггер  \rs_триггер_1  (.S(D), .c(c), .R(not_1_out), .Reset(Reset), .nQ(nQ), .Q(Q));
endmodule

// RS
module \RS_триггер  (
  input  S,
  input  c,
  input  R,
  input  Reset,
  output nQ,
  output Q
);

  wire and_1_out, and_2_out;

  and and_1 (and_1_out, S, c);
  and and_2 (and_2_out, c, R);
  nor nor_1 (nQ, and_1_out, Q);
  nor nor_2 (Q, nQ, Reset, and_2_out);
endmodule

module \Динамический_D_триггер  (
  input  D,
  input  \с ,
  input  Reset,
  output nQ,
  output Q
);

  wire \d_триггер_1_q , not_1_out;

  \D_триггер  \d_триггер_1  (.D(D), .c(\с ), .Reset(Reset), .Q(\d_триггер_1_q ));  // open: nQ
  not not_1 (not_1_out, \с );
  \D_триггер  \d_триггер_2  (.D(\d_триггер_1_q ), .c(not_1_out), .Reset(Reset), .nQ(nQ), .Q(Q));
endmodule

module \T_триггер  (
  input  T,
  input  Reset,
  output nQ,
  output Q
);

  \Динамический_D_триггер  \u_динамический_d_триггер_1  (.D(nQ), .\с (T), .Reset(Reset), .nQ(nQ), .Q(Q));
endmodule

module \Реверсивный_счётчик  (
  input  plus_1,
  input  minus_1,
  input  N,
  input  Reset,
  output Q,
  output nQ
);

  wire and_1_out, and_2_out, or_1_out;

  and and_1 (and_1_out, plus_1, ~N);  // AND_Gate
  and and_2 (and_2_out, N, minus_1);
  or or_1 (or_1_out, and_1_out, and_2_out);
  \T_триггер  \t_триггер_1  (.T(or_1_out), .Reset(Reset), .nQ(Q), .Q(nQ));
endmodule

module \Рабочий_Суммирующий_счетчик  (
  input  N,
  input  in_2,
  output q0,
  output q1,
  output q2,
  output q3,
  output q4
);

  wire and_1_out, and_2_out, and_3_out, and_4_out, and_5_out, and_6_out, buffer_1_out, or_1_out, plus_1_out,
       Reset_out;

  Button plus_1 (.out(plus_1_out));
  Button Reset (.out(Reset_out));
  or or_1 (or_1_out, Reset_out, and_6_out);
  and and_1 (and_1_out, plus_1_out, ~N);  // AND_Gate
  buf buffer_1 (buffer_1_out, or_1_out);
  T_Flip_Flop #(.trigger("falling")) t_ff_1 (
    .clk(and_1_out), .T(in_2), .Q(q0), .reset(buffer_1_out));  // open: Qn, preset, en
  and and_2 (and_2_out, q0, ~N);  // AND_Gate
  T_Flip_Flop #(.trigger("falling")) t_ff_2 (
    .clk(and_2_out), .T(in_2), .Q(q1), .reset(buffer_1_out));  // open: Qn, preset, en
  and and_3 (and_3_out, q1, ~N);  // AND_Gate
  T_Flip_Flop #(.trigger("falling")) t_ff_3 (
    .clk(and_3_out), .T(in_2), .Q(q2), .reset(buffer_1_out));  // open: Qn, preset, en
  and and_4 (and_4_out, q2, ~N);  // AND_Gate
  T_Flip_Flop #(.trigger("falling")) t_ff_4 (
    .clk(and_4_out), .T(in_2), .Q(q3), .reset(buffer_1_out));  // open: Qn, preset, en
  and and_5 (and_5_out, q3, ~N);  // AND_Gate
  T_Flip_Flop #(.trigger("falling")) t_ff_5 (
    .clk(and_5_out), .T(in_2), .Q(q4), .reset(buffer_1_out));  // open: Qn, preset, en
  and and_6 (and_6_out, q4, q1);
endmodule
